# Fritzing sketch aProjector (saved by Fritzing 0.9.3b)
breadboards: 1

parts:
  Mod1 = MSP-EXP432P401R_EagleCAD
  hc-sr1 = hc-sr04
  R1 = Resistor [tolerance=±5% resistance=2.2k package="0603 [SMD]"]
  R2 = Resistor [tolerance=±5% resistance=3.3k package="0603 [SMD]"]
  Pololu_A1 = Pololu A4988 [package=SO16]
  SW1 = DIP SWITCH [package=dipswitch-02]
  M1 = Stepper Motor - Bipolar
  VCC1 = Battery block 9V
  C1 = Electrolytic Capacitor [capacitance=10µF package="100 mil [THT, electrolytic]"]
  VCC2 = Battery
  R3 = Resistor [tolerance=±5% resistance=220 package="0603 [SMD]"]

nets:
  +3V3: Mod1.+3V3, Mod1.3V3, Pololu_A1.VDD, SW1.4
  N1: Mod1.P4.1, SW1.1, R3.Pin_0
  GND: Mod1.GND, Mod1.DEBUG_P_GND, hc-sr1.GND, R2.Pin_1, Pololu_A1.GND#8, R3.Pin_1
  5V: Mod1.5V, hc-sr1.VCC
  N2: Mod1.P2.4, Mod1.P7.3, R1.Pin_1, R2.Pin_0
  N3: Mod1.P5.1, Pololu_A1.DIR
  N4: Mod1.P2.5, hc-sr1.Trig
  N5: Mod1.P5.0, Pololu_A1.STEP
  N6: hc-sr1.Echo, R1.Pin_0
  N7: Pololu_A1.RESET, Pololu_A1.SLEEP
  N8: Pololu_A1.1B, M1.D
  N9: Pololu_A1.1A, M1.B
  N10: Pololu_A1.2A, M1.C
  N11: Pololu_A1.2B, M1.A
  N12: Pololu_A1.GND#14, C1.-, VCC2.-
  N13: Pololu_A1.VMOT, VCC1.+, C1.+
  N14: VCC1.-, VCC2.+

custom parts:
  MSP-EXP432P401R_EagleCAD: TI Launch pad MSP-EXP432P401R development board.
